// Digital circuit simulation.dig as structural Verilog
module simulation (
  input  NE555,
  input  not_LPC_L,
  input  not_LPC_H,
  input  not_EPC_L,
  input  not_EPC_H,
  output CLR,
  output not_CLR,
  output CLK,
  output not_CLK,
  output CPC,
  output LIR,
  output not_ERAM,
  output not_EPC_RAM,
  output not_NOP,
  output LACC,
  output not_EACC,
  output not_HLT,
  output LMAR_L,
  output LMAR_H,
  output not_EMAR,
  output out_21,
  output out_22,
  output out_23,
  output out_24,
  output out_25
);

  wire _7408_1_pin8, CLOCK_BUF_C27_pin2, CLOCK_BUF_C27_pin12, CLOCK_BUF_C27_pin13, Control_Word__2_p5,
       Control_Word__2_p7, Control_Word__2_p9, Control_Word__2_p10, Control_Word__2_p11, Control_Word__2_p13,
       Control_Word__2_p14, Control_Word__2_p15, Control_Word__2_p16, Control_Word__2_p17,
       Control_Word__2_p18, Control_Word__2_p19, Control_Word__2_p20, Debouncer_C24_pin8,
       Debouncer_C24_pin10, Debouncer_C26_pin2, Debouncer_C26_pin3, Debouncer_C26_pin8, Debouncer_C26_pin10,
       Debouncer_C26_pin11, Debouncer_C26_pin12, IR_pin3, IR_pin4, IR_pin7, IR_pin8, IR_pin13, IR_pin14,
       IR_pin17, IR_pin18, MAR_H_pin2, MAR_H_pin5, MAR_H_pin6, MAR_H_pin9, MAR_H_pin12, MAR_H_pin15,
       MAR_H_pin16, MAR_L_pin2, MAR_L_pin5, MAR_L_pin6, MAR_L_pin9, MAR_L_pin12, MAR_L_pin15, MAR_L_pin16,
       MAR_L_pin19, PC_HH_pin11, PC_HH_pin12, PC_HH_pin13, PC_HH_pin14, PC_HL_pin11, PC_HL_pin12,
       PC_HL_pin13, PC_HL_pin14, PC_HL_pin15, PC_LH_pin11, PC_LH_pin12, PC_LH_pin13, PC_LH_pin14,
       PC_LH_pin15, PC_LL_pin11, PC_LL_pin12, PC_LL_pin13, PC_LL_pin14, PC_LL_pin15, PUSH_CLEAR_p2,
       PUSH_CLEAR_p3, PUSH_SINGLE_STEP_p2, PUSH_SINGLE_STEP_p3, SW_MANUAL_AUTO_p2, SW_MANUAL_AUTO_p3;

  // SwitchDT PUSH_SINGLE_STEP: pin names not known; wires that end beside it: 1'b0, PUSH_SINGLE_STEP_p2, PUSH_SINGLE_STEP_p3
  // SwitchDT SW_MANUAL_AUTO: pin names not known; wires that end beside it: 1'b0, SW_MANUAL_AUTO_p2, SW_MANUAL_AUTO_p3
  // _28c64 Control_Word__2: pin names not known; wires that end beside it: 1'b0, not_EMAR, LMAR_H, LMAR_L, Control_Word__2_p5, out_25, Control_Word__2_p7, 1'b0, Control_Word__2_p9, Control_Word__2_p10, Control_Word__2_p11, 1'b0, Control_Word__2_p13, Control_Word__2_p14, Control_Word__2_p15, Control_Word__2_p16, Control_Word__2_p17, Control_Word__2_p18, Control_Word__2_p19, Control_Word__2_p20, 1'b1, 1'b1, 1'b0, not_EPC_RAM
  _7408 _7408_1 (
    .pin1(1'b0), .pin2(1'b0), .pin4(1'b0), .pin5(1'b0), .pin7(1'b0), .pin8(_7408_1_pin8), .pin9(not_NOP),
    .pin10(not_CLR), .pin12(1'b1), .pin13(1'b1), .pin14(1'b1));  // open: pin3, pin6, pin11
  // SwitchDT PUSH_CLEAR: pin names not known; wires that end beside it: 1'b0, PUSH_CLEAR_p2, PUSH_CLEAR_p3
  _74590 _74590_1 (
    .pin1(Control_Word__2_p7), .pin2(Control_Word__2_p9), .pin3(Control_Word__2_p11),
    .pin4(Control_Word__2_p13), .pin8(1'b0), .pin10(_7408_1_pin8), .pin11(not_CLK), .pin12(1'b0),
    .pin13(CLK), .pin14(1'b0), .pin15(Control_Word__2_p5), .pin16(1'b1));  // open: pin5, pin6, pin7, pin9
  PullUp pullup_1 (.out(PUSH_CLEAR_p2));
  PullUp pullup_2 (.out(PUSH_CLEAR_p3));
  PullUp pullup_3 (.out(PUSH_SINGLE_STEP_p3));
  PullUp pullup_4 (.out(PUSH_SINGLE_STEP_p2));
  PullUp pullup_5 (.out(SW_MANUAL_AUTO_p3));
  PullUp pullup_6 (.out(SW_MANUAL_AUTO_p2));
  _7400 Debouncer_C24 (
    .pin1(PUSH_CLEAR_p2), .pin2(CLR), .pin3(not_CLR), .pin4(not_CLR), .pin5(PUSH_CLEAR_p3), .pin6(CLR),
    .pin7(1'b0), .pin8(Debouncer_C24_pin8), .pin9(PUSH_SINGLE_STEP_p3), .pin10(Debouncer_C24_pin10),
    .pin11(Debouncer_C24_pin10), .pin12(Debouncer_C24_pin8), .pin13(PUSH_SINGLE_STEP_p2), .pin14(1'b1));
  _7400 Debouncer_C26 (
    .pin1(SW_MANUAL_AUTO_p2), .pin2(Debouncer_C26_pin2), .pin3(Debouncer_C26_pin3),
    .pin4(Debouncer_C26_pin3), .pin5(SW_MANUAL_AUTO_p3), .pin6(Debouncer_C26_pin2), .pin7(1'b0),
    .pin8(Debouncer_C26_pin8), .pin9(Debouncer_C26_pin2), .pin10(Debouncer_C26_pin10),
    .pin11(Debouncer_C26_pin11), .pin12(Debouncer_C26_pin12), .pin13(Debouncer_C26_pin8), .pin14(1'b1));
  // _28c64 Control_Word__1: pin names not known; wires that end beside it: not_ERAM, LIR, Control_Word__2_p5, not_NOP, Control_Word__2_p7, 1'b0, Control_Word__2_p9, Control_Word__2_p10, Control_Word__2_p11, 1'b0, Control_Word__2_p13, Control_Word__2_p14, Control_Word__2_p15, Control_Word__2_p16, Control_Word__2_p17, Control_Word__2_p18, Control_Word__2_p19, Control_Word__2_p20, 1'b1, 1'b1
  _7410 C25 (
    .pin1(not_HLT), .pin2(Debouncer_C24_pin10), .pin3(1'b1), .pin4(1'b1), .pin5(1'b1), .pin7(1'b0),
    .pin9(1'b1), .pin10(1'b1), .pin11(1'b1), .pin12(Debouncer_C26_pin12), .pin13(Debouncer_C26_pin3),
    .pin14(1'b1));  // open: pin6, pin8
  _74107 C29 (
    .pin1(not_HLT), .pin3(Debouncer_C26_pin10), .pin4(not_HLT), .pin7(1'b0), .pin8(1'b0), .pin9(1'b0),
    .pin10(1'b0), .pin11(1'b0), .pin12(NE555), .pin13(not_CLR), .pin14(1'b1));  // open: pin2, pin5, pin6
  _7404 CLOCK_BUF_C27 (
    .pin1(Debouncer_C26_pin11), .pin2(CLOCK_BUF_C27_pin2), .pin3(CLOCK_BUF_C27_pin2), .pin4(CLK),
    .pin5(Debouncer_C26_pin11), .pin6(not_CLK), .pin7(1'b0), .pin9(1'b1), .pin11(1'b1),
    .pin12(CLOCK_BUF_C27_pin12), .pin13(CLOCK_BUF_C27_pin13), .pin14(1'b1));  // open: pin8, pin10
  _74373 IR (
    .pin1(1'b0), .pin2(Control_Word__2_p15), .pin3(IR_pin3), .pin4(IR_pin4), .pin5(Control_Word__2_p17),
    .pin6(Control_Word__2_p19), .pin7(IR_pin7), .pin8(IR_pin8), .pin9(Control_Word__2_p18), .pin10(1'b0),
    .pin11(LIR), .pin12(Control_Word__2_p16), .pin13(IR_pin13), .pin14(IR_pin14),
    .pin15(Control_Word__2_p10), .pin16(Control_Word__2_p14), .pin17(IR_pin17), .pin18(IR_pin18),
    .pin19(Control_Word__2_p20), .pin20(1'b1));
  _74373 ACC (
    .pin1(not_EACC), .pin2(IR_pin3), .pin3(IR_pin3), .pin4(IR_pin4), .pin5(IR_pin4), .pin6(IR_pin7),
    .pin7(IR_pin7), .pin8(IR_pin8), .pin9(IR_pin8), .pin10(1'b0), .pin11(LACC), .pin12(IR_pin13),
    .pin13(IR_pin13), .pin14(IR_pin14), .pin15(IR_pin14), .pin16(IR_pin17), .pin17(IR_pin17),
    .pin18(IR_pin18), .pin19(IR_pin18), .pin20(1'b1));
  _74163 PC_LL (
    .pin1(not_CLR), .pin2(not_CLK), .pin3(IR_pin3), .pin4(IR_pin4), .pin5(IR_pin7), .pin6(IR_pin8),
    .pin7(CPC), .pin8(1'b0), .pin9(not_LPC_L), .pin10(1'b1), .pin11(PC_LL_pin11), .pin12(PC_LL_pin12),
    .pin13(PC_LL_pin13), .pin14(PC_LL_pin14), .pin15(PC_LL_pin15), .pin16(1'b1));
  _74163 PC_LH (
    .pin1(not_CLR), .pin2(not_CLK), .pin3(IR_pin13), .pin4(IR_pin14), .pin5(IR_pin17), .pin6(IR_pin18),
    .pin7(CPC), .pin8(1'b0), .pin9(not_LPC_L), .pin10(PC_LL_pin15), .pin11(PC_LH_pin11), .pin12(PC_LH_pin12),
    .pin13(PC_LH_pin13), .pin14(PC_LH_pin14), .pin15(PC_LH_pin15), .pin16(1'b1));
  _74163 PC_HL (
    .pin1(not_CLR), .pin2(not_CLK), .pin3(IR_pin3), .pin4(IR_pin4), .pin5(IR_pin7), .pin6(IR_pin8),
    .pin7(CPC), .pin8(1'b0), .pin9(not_LPC_H), .pin10(PC_LH_pin15), .pin11(PC_HL_pin11), .pin12(PC_HL_pin12),
    .pin13(PC_HL_pin13), .pin14(PC_HL_pin14), .pin15(PC_HL_pin15), .pin16(1'b1));
  _74163 PC_HH (
    .pin1(not_CLR), .pin2(not_CLK), .pin3(IR_pin13), .pin4(IR_pin14), .pin5(IR_pin17), .pin6(IR_pin18),
    .pin7(CPC), .pin8(1'b0), .pin9(not_LPC_H), .pin10(PC_HL_pin15), .pin11(PC_HH_pin11), .pin12(PC_HH_pin12),
    .pin13(PC_HH_pin13), .pin14(PC_HH_pin14), .pin16(1'b1));  // open: pin15
  _74373 MAR_L (
    .pin1(not_EMAR), .pin2(MAR_L_pin2), .pin3(IR_pin3), .pin4(IR_pin4), .pin5(MAR_L_pin5), .pin6(MAR_L_pin6),
    .pin7(IR_pin7), .pin8(IR_pin8), .pin9(MAR_L_pin9), .pin10(1'b0), .pin11(LMAR_L), .pin12(MAR_L_pin12),
    .pin13(IR_pin13), .pin14(IR_pin14), .pin15(MAR_L_pin15), .pin16(MAR_L_pin16), .pin17(IR_pin17),
    .pin18(IR_pin18), .pin19(MAR_L_pin19), .pin20(1'b1));
  _74373 MAR_H (
    .pin1(not_EMAR), .pin2(MAR_H_pin2), .pin3(IR_pin3), .pin4(IR_pin4), .pin5(MAR_H_pin5), .pin6(MAR_H_pin6),
    .pin7(IR_pin7), .pin8(IR_pin8), .pin9(MAR_H_pin9), .pin10(1'b0), .pin11(LMAR_H), .pin12(MAR_H_pin12),
    .pin13(IR_pin13), .pin14(IR_pin14), .pin15(MAR_H_pin15), .pin16(MAR_H_pin16), .pin17(IR_pin17),
    .pin18(IR_pin18), .pin19(CLOCK_BUF_C27_pin13), .pin20(1'b1));
  _74245 _74245_1 (
    .pin1(1'b1), .pin2(PC_LL_pin14), .pin3(PC_LL_pin13), .pin4(PC_LL_pin12), .pin5(PC_LL_pin11),
    .pin6(PC_LH_pin14), .pin7(PC_LH_pin13), .pin8(PC_LH_pin12), .pin9(PC_LH_pin11), .pin10(1'b0),
    .pin11(IR_pin18), .pin12(IR_pin17), .pin13(IR_pin14), .pin14(IR_pin13), .pin15(IR_pin8), .pin16(IR_pin7),
    .pin17(IR_pin4), .pin18(IR_pin3), .pin19(not_EPC_L), .pin20(1'b1));
  _74245 _74245_2 (
    .pin1(1'b1), .pin2(PC_HL_pin14), .pin3(PC_HL_pin13), .pin4(PC_HL_pin12), .pin5(PC_HL_pin11),
    .pin6(PC_HH_pin14), .pin7(PC_HH_pin13), .pin8(PC_HH_pin12), .pin9(PC_HH_pin11), .pin10(1'b0),
    .pin11(IR_pin18), .pin12(IR_pin17), .pin13(IR_pin14), .pin14(IR_pin13), .pin15(IR_pin8), .pin16(IR_pin7),
    .pin17(IR_pin4), .pin18(IR_pin3), .pin19(not_EPC_H), .pin20(1'b1));
  _74245 _74245_3 (
    .pin1(1'b1), .pin2(PC_LL_pin14), .pin3(PC_LL_pin13), .pin4(PC_LL_pin12), .pin5(PC_LL_pin11),
    .pin6(PC_LH_pin14), .pin7(PC_LH_pin13), .pin8(PC_LH_pin12), .pin9(PC_LH_pin11), .pin10(1'b0),
    .pin11(MAR_L_pin19), .pin12(MAR_L_pin16), .pin13(MAR_L_pin15), .pin14(MAR_L_pin12), .pin15(MAR_L_pin9),
    .pin16(MAR_L_pin6), .pin17(MAR_L_pin5), .pin18(MAR_L_pin2), .pin19(not_EPC_RAM), .pin20(1'b1));
  _74245 _74245_4 (
    .pin1(1'b1), .pin2(PC_HL_pin14), .pin3(PC_HL_pin13), .pin4(PC_HL_pin12), .pin5(PC_HL_pin11),
    .pin6(PC_HH_pin14), .pin7(PC_HH_pin13), .pin8(PC_HH_pin12), .pin9(PC_HH_pin11), .pin10(1'b0),
    .pin11(CLOCK_BUF_C27_pin13), .pin12(MAR_H_pin16), .pin13(MAR_H_pin15), .pin14(MAR_H_pin12),
    .pin15(MAR_H_pin9), .pin16(MAR_H_pin6), .pin17(MAR_H_pin5), .pin18(MAR_H_pin2), .pin19(not_EPC_RAM),
    .pin20(1'b1));
  // _28c256 ROM: pin names not known; wires that end beside it: MAR_H_pin16, MAR_H_pin12, MAR_L_pin19, MAR_L_pin16, MAR_L_pin15, MAR_L_pin12, MAR_L_pin9, MAR_L_pin6, MAR_L_pin5, MAR_L_pin2, IR_pin3, IR_pin4, IR_pin7, 1'b0, 1'b1, 1'b1, MAR_H_pin15, MAR_H_pin2, MAR_H_pin5, MAR_H_pin9, not_ERAM, MAR_H_pin6, CLOCK_BUF_C27_pin13, IR_pin18
  // _62256 RAM: pin names not known; wires that end beside it: MAR_H_pin16, MAR_H_pin12, MAR_L_pin19, MAR_L_pin16, MAR_L_pin15, MAR_L_pin12, MAR_L_pin9, MAR_L_pin6, MAR_L_pin5, MAR_L_pin2, IR_pin3, IR_pin4, IR_pin7, 1'b0, 1'b1, 1'b1, MAR_H_pin15, MAR_H_pin2, MAR_H_pin5, MAR_H_pin9, not_ERAM, MAR_H_pin6, CLOCK_BUF_C27_pin12, IR_pin18

  // Notes on the sheet:
  //   not_LPC_L: default 1
  //   not_LPC_H: default 1
  //   not_EPC_L: default 1
  //   not_EPC_H: default 1
  //   contents of Control Word #2 (hex, n*v repeats v):
  //   /Users/Vittorio.Nardone/Documents/__private__/sap-project/roms/cw2-rom.hex false
  //   contents of ROM (hex, n*v repeats v):
  //   /Users/Vittorio.Nardone/Documents/__private__/sap-project/roms/kernel-rom.hex false
  //   contents of Control Word #1 (hex, n*v repeats v):
  //   /Users/Vittorio.Nardone/Documents/__private__/sap-project/roms/cw1-rom.hex false
endmodule
